# Fritzing sketch analogSwitchCircuit (saved by Fritzing 0.9.3b)
circuit board: 8.82076cm x 3.77284cm
stripboards: 1

parts:
  S1 = Pushbutton [package="[SMD]"]
  S2 = Pushbutton [package="[SMD]"]
  S3 = Pushbutton [package="[SMD]"]
  S4 = Pushbutton [package="[SMD]"]
  R1 = Resistor [tolerance=±5% resistance=1M package=THT]
  R2 = Resistor [tolerance=±5% resistance=470k package=THT]
  R3 = Resistor [tolerance=±5% resistance=100k package=THT]
  R4 = Resistor [tolerance=±5% resistance=47k package=THT]
  R5 = Resistor [tolerance=±5% resistance=10k package=THT]
  Bela_Analog_In = female pin header, 1 pin [form="♀ (female)"]

nets:
  N1: S1.Pin_1, S1.Pin_2, S2.Pin_1, S2.Pin_2, S3.Pin_1, S3.Pin_2, S4.Pin_1, S4.Pin_2, R5.Pin_0, Bela_Analog_In.pin1
  N2: S1.Pin_3, S1.Pin_4, R1.Pin_1
  N3: S2.Pin_3, S2.Pin_4, R2.Pin_1
  N4: S3.Pin_3, S3.Pin_4, R3.Pin_0
  N5: S4.Pin_3, S4.Pin_4, R4.Pin_0
  5V: R1.Pin_0, R2.Pin_0, R3.Pin_1, R4.Pin_1
  GND: R5.Pin_1
