# Fritzing sketch prototypeCircuitTest (saved by Fritzing 0.9.3b)
circuit board: 9cm x 8cm
stripboards: 1

parts:
  R6 = Resistor [tolerance=±5% resistance=10k package=THT]
  R7 = Resistor [tolerance=±5% resistance=10k package=THT]
  R8 = Resistor [tolerance=±5% resistance=10k package=THT]
  R9 = Resistor [tolerance=±5% resistance=10k package=THT]
  R11 = Resistor [tolerance=±5% resistance=100k package=THT]
  R12 = Resistor [tolerance=±5% resistance=470k package=THT]
  R13 = Resistor [tolerance=±5% resistance=1M package=THT]
  R14 = Resistor [tolerance=±5% resistance=47k package=THT]
  R15 = Resistor [tolerance=±5% resistance=100k package=THT]
  R16 = Resistor [tolerance=±5% resistance=470k package=THT]
  R17 = Resistor [tolerance=±5% resistance=1M package=THT]
  R18 = Resistor [tolerance=±5% resistance=10k package=THT]
  R19 = Resistor [tolerance=±5% resistance=10k package=THT]
  LED1 = LED - 5mm [color="Red (633nm)" package="5 mm [THT]"]
  R20 = Resistor [tolerance=±5% resistance=470k package=THT]
  LED2 = LED - 5mm [color="Red (633nm)" package="5 mm [THT]"]
  R21 = Resistor [tolerance=±5% resistance=470k package=THT]
  R22 = Resistor [tolerance=±5% resistance=470k package=THT]
  LED3 = LED - 5mm [color="Red (633nm)" package="5 mm [THT]"]
  R23 = Resistor [tolerance=±5% resistance=470k package=THT]
  LED4 = LED - 5mm [color="Red (633nm)" package="5 mm [THT]"]
  R24 = Resistor [tolerance=±5% resistance=470k package=THT]
  LED5 = LED - 5mm [color="Red (633nm)" package="5 mm [THT]"]
  R25 = Resistor [tolerance=±5% resistance=470k package=THT]
  LED6 = LED - 5mm [color="Red (633nm)" package="5 mm [THT]"]
  R26 = Resistor [tolerance=±5% resistance=470k package=THT]
  LED7 = LED - 5mm [color="Red (633nm)" package="5 mm [THT]"]
  R31 = Trimmer Potentiometer [maximum_resistance=1k package=THT]
  R29 = Trimmer Potentiometer [maximum_resistance=1k package=THT]
  R30 = Trimmer Potentiometer [maximum_resistance=1k package=THT]
  S17 = Pushbutton [package="[THT]"]
  S16 = Pushbutton [package="[THT]"]
  S15 = Pushbutton [package="[THT]"]
  S14 = Pushbutton [package="[THT]"]
  S18 = Pushbutton [package="[THT]"]
  S19 = Pushbutton [package="[THT]"]
  S20 = Pushbutton [package="[THT]"]
  S21 = Pushbutton [package="[THT]"]
  S22 = Pushbutton [package="[THT]"]
  S23 = Pushbutton [package="[THT]"]
  S24 = Pushbutton [package="[THT]"]
  S25 = Pushbutton [package="[THT]"]
  LED8 = LED - 5mm [color="Red (633nm)" package="5 mm [THT]"]
  R27 = Resistor [tolerance=±5% resistance=470k package=THT]
  J19 = female pin header, 1 pin [form="♀ (female)"]
  J2 = female pin header, 1 pin [form="♀ (female)"]
  J20 = female pin header, 1 pin [form="♀ (female)"]
  J16 = female pin header, 1 pin [form="♀ (female)"]
  J15 = female pin header, 1 pin [form="♀ (female)"]
  J17 = female pin header, 1 pin [form="♀ (female)"]
  J10 = female pin header, 1 pin [form="♀ (female)"]
  J11 = female pin header, 1 pin [form="♀ (female)"]
  J5 = female pin header, 1 pin [form="♀ (female)"]
  J1 = female pin header, 1 pin [form="♀ (female)"]
  J18 = female pin header, 1 pin [form="♀ (female)"]
  J6 = female pin header, 1 pin [form="♀ (female)"]
  J14 = female pin header, 1 pin [form="♀ (female)"]
  J12 = female pin header, 1 pin [form="♀ (female)"]
  J21 = female pin header, 1 pin [form="♀ (female)"]
  J13 = female pin header, 1 pin [form="♀ (female)"]
  J22 = female pin header, 1 pin [form="♀ (female)"]
  J23 = female pin header, 1 pin [form="♀ (female)"]
  R28 = Trimmer Potentiometer [maximum_resistance=1k package=THT]
  R10 = Resistor [tolerance=±5% resistance=47k package=THT]
  J24 = female pin header, 1 pin [form="♀ (female)"]
  J25 = female pin header, 1 pin [form="♀ (female)"]

nets:
  GND: R6.Pin_0, R7.Pin_0, R8.Pin_0, R9.Pin_0, R18.Pin_1, R19.Pin_1, LED1.cathode, LED2.cathode, LED3.cathode, LED4.cathode, LED5.cathode, LED6.cathode, LED7.cathode, R31.leg2, R29.leg2, R30.leg2, LED8.cathode, R28.leg2, J25.pin1
  N1: R6.Pin_1, S14.Pin_1, S14.Pin_2, J6.pin1
  N2: R7.Pin_1, S17.Pin_1, S17.Pin_2, J1.pin1
  N3: R8.Pin_1, S15.Pin_1, S15.Pin_2, J18.pin1
  N4: R9.Pin_1, S16.Pin_1, S16.Pin_2, J5.pin1
  5V: R11.Pin_0, R12.Pin_1, R13.Pin_1, R14.Pin_1, R15.Pin_1, R16.Pin_0, R17.Pin_0, R31.leg1, R29.leg1, R30.leg1, S17.Pin_3, S17.Pin_4, S16.Pin_3, S16.Pin_4, S15.Pin_3, S15.Pin_4, S14.Pin_3, S14.Pin_4, R28.leg1, R10.Pin_0, J24.pin1
  N5: R11.Pin_1, S19.Pin_3, S19.Pin_4
  N6: R12.Pin_0, S20.Pin_3, S20.Pin_4
  N7: R13.Pin_0, S21.Pin_3, S21.Pin_4
  N8: R14.Pin_0, S22.Pin_3, S22.Pin_4
  N9: R15.Pin_0, S23.Pin_3, S23.Pin_4
  N10: R16.Pin_1, S24.Pin_3, S24.Pin_4
  N11: R17.Pin_1, S25.Pin_3, S25.Pin_4
  N12: R18.Pin_0, S18.Pin_1, S18.Pin_2, S19.Pin_1, S19.Pin_2, S20.Pin_1, S20.Pin_2, S21.Pin_1, S21.Pin_2, J14.pin1
  N13: R19.Pin_0, S22.Pin_1, S22.Pin_2, S23.Pin_1, S23.Pin_2, S24.Pin_1, S24.Pin_2, S25.Pin_1, S25.Pin_2, J23.pin1
  N14: LED1.anode, R20.Pin_0
  N15: R20.Pin_1, J12.pin1
  N16: LED2.anode, R21.Pin_0
  N17: R21.Pin_1, J21.pin1
  N18: R22.Pin_0, LED3.anode
  N19: R22.Pin_1, J13.pin1
  N20: R23.Pin_0, LED4.anode
  N21: R23.Pin_1, J22.pin1
  N22: R24.Pin_0, LED5.anode
  N23: R24.Pin_1, J19.pin1
  N24: R25.Pin_0, LED6.anode
  N25: R25.Pin_1, J2.pin1
  N26: R26.Pin_0, J11.pin1
  N27: R26.Pin_1, LED7.anode
  N28: R31.wiper, J17.pin1
  N29: R29.wiper, J16.pin1
  N30: R30.wiper, J10.pin1
  N31: S18.Pin_3, S18.Pin_4, R10.Pin_1
  N32: LED8.anode, R27.Pin_1
  N33: R27.Pin_0, J20.pin1
  N34: J15.pin1, R28.wiper
